// Logisim project 2cpu.circ as structural Verilog: 1 circuit, main circuit main
module main (
);

  wire [0:0] undriven_2;
  wire [3:0] undriven;

  // DipSwitch dipswitch_1: pin names not known
  // AND_Gate load has open pins: in0=undriven[0], in1=undriven[1], in2=undriven[2], in3=undriven[3], out=open
  D_Flip_Flop d_ff_1 (.D(undriven_2[0]));  // open: clk, Q, Qn, preset, reset
  D_Flip_Flop d_ff_2 ();  // open: D, clk, Q, Qn, preset, reset
  D_Flip_Flop d_ff_3 ();  // open: D, clk, Q, Qn, preset, reset
  D_Flip_Flop d_ff_4 ();  // open: D, clk, Q, Qn, preset, reset
endmodule
