// Logisim project CPU_TTL_AGAON.circ as structural Verilog: 1 circuit, main circuit main
module main (
);

  wire clock_1_out, dipswitch_1_p1, dipswitch_1_p2, dipswitch_1_p3, dipswitch_1_p4, n74283_1_pin7;
  wire [3:0] n74175_1_pin2, n74175_2_pin2, n74283_1_pin4;

  // DipSwitch dipswitch_1: pin names not known; wires that end beside it: dipswitch_1_p1, dipswitch_1_p2, dipswitch_1_p3, dipswitch_1_p4
  Clock clock_1 (.out(clock_1_out));
  Pull_Resistor pull_resistor_1 (.node(dipswitch_1_p1));
  Pull_Resistor pull_resistor_2 (.node(dipswitch_1_p2));
  Pull_Resistor pull_resistor_3 (.node(dipswitch_1_p3));
  Pull_Resistor pull_resistor_4 (.node(dipswitch_1_p4));
  _74245 #(.ShowInternalStructure("true")) u_74245_1 ();  // open: pin1, pin2, pin3, pin4, pin5, pin6, pin7, pin8, pin9, pin19, pin18, pin17, pin16, pin15, pin14, pin13, pin12, pin11
  _74175 u_74175_1 (
    .pin2(n74175_1_pin2[0]), .pin4(dipswitch_1_p4), .pin5(dipswitch_1_p3), .pin7(n74175_1_pin2[1]),
    .pin15(n74175_1_pin2[3]), .pin13(dipswitch_1_p1), .pin12(dipswitch_1_p2), .pin10(n74175_1_pin2[2]),
    .pin9(clock_1_out));  // open: pin1, pin3, pin6, pin14, pin11
  _74175 u_74175_2 (
    .pin2(n74175_2_pin2[0]), .pin4(dipswitch_1_p4), .pin5(dipswitch_1_p3), .pin7(n74175_2_pin2[1]),
    .pin15(n74175_2_pin2[3]), .pin13(dipswitch_1_p1), .pin12(dipswitch_1_p2), .pin10(n74175_2_pin2[2]),
    .pin9(clock_1_out));  // open: pin1, pin3, pin6, pin14, pin11
  _74283 u_74283_1 (
    .pin1(n74283_1_pin4[1]), .pin2(n74175_2_pin2[1]), .pin3(n74175_1_pin2[1]), .pin4(n74283_1_pin4[0]),
    .pin5(n74175_1_pin2[0]), .pin6(n74175_2_pin2[0]), .pin7(n74283_1_pin7), .pin15(n74175_2_pin2[2]),
    .pin14(n74175_1_pin2[2]), .pin13(n74283_1_pin4[2]), .pin12(n74175_1_pin2[3]), .pin11(n74175_2_pin2[3]),
    .pin10(n74283_1_pin4[3]));  // open: pin9
  Pull_Resistor pull_resistor_5 (.node(n74283_1_pin7));
  Hex_Digit_Display hex_digit_display_1 (.value(n74283_1_pin4));  // open: dp
endmodule
