// Logisim project MyCpi.circ as structural Verilog: 1 circuit, main circuit main
module main (
);

  wire and_1_out, and_2_out, and_3_out, and_4_out, and_5_out, and_6_out, and_7_out, and_8_out, and_13_out,
       and_14_out, and_15_out, and_16_out, and_17_out, and_18_out, and_19_out, and_20_out, and_25_out,
       and_26_out, and_27_out, and_28_out, and_29_out, and_30_out, and_31_out, and_32_out, and_37_out,
       and_38_out, and_39_out, and_40_out, and_41_out, and_42_out, and_43_out, and_44_out, button_1_out,
       d_ff_1_q, d_ff_2_q, d_ff_3_q, d_ff_4_q, d_ff_5_q, d_ff_6_q, d_ff_7_q, d_ff_8_q, d_ff_9_q, d_ff_10_q,
       d_ff_11_q, d_ff_12_q, d_ff_13_q, d_ff_14_q, d_ff_15_q, d_ff_16_q, decoder_1_out0, decoder_1_out1,
       decoder_1_out2, decoder_1_out3, demultiplexer_1_out0, demultiplexer_1_out1, demultiplexer_1_out2,
       demultiplexer_1_out3, dipswitch_1_p1, dipswitch_1_p2, dipswitch_1_p3, dipswitch_2_p1, dipswitch_2_p4,
       dipswitch_2_p5, not_1_out, not_2_out, not_3_out, not_4_out, not_5_out, undriven, undriven_2,
       undriven_3, undriven_4, undriven_5, undriven_6, undriven_7, undriven_8;
  wire [1:0] dipswitch_2_p3;
  wire [3:0] and_9_out;

  Button button_1 (.out(button_1_out));
  // DipSwitch #(.number(4)) dipswitch_1: pin names not known; wires that end beside it: dipswitch_1_p1, dipswitch_1_p2, dipswitch_1_p3
  // DipSwitch #(.number(4)) dipswitch_2: pin names not known; wires that end beside it: dipswitch_2_p1, dipswitch_2_p3[1], dipswitch_2_p3[0], dipswitch_2_p4, dipswitch_2_p5
  not not_1 (not_1_out, dipswitch_2_p5);
  Decoder #(.select(2)) decoder_1 (
    .out0(decoder_1_out0), .out1(decoder_1_out1), .out2(decoder_1_out2), .out3(decoder_1_out3),
    .sel(dipswitch_2_p3), .en(dipswitch_2_p4));
  Demultiplexer #(.select(2)) demultiplexer_1 (
    .out0(demultiplexer_1_out0), .out1(demultiplexer_1_out1), .out2(demultiplexer_1_out2),
    .out3(demultiplexer_1_out3), .in(button_1_out), .sel(dipswitch_2_p3));
  and and_1 (and_1_out, not_1_out, dipswitch_2_p1);
  and and_2 (and_2_out, not_1_out, dipswitch_1_p3);
  and and_3 (and_3_out, not_1_out, dipswitch_1_p2);
  and and_4 (and_4_out, not_1_out, dipswitch_1_p1);
  and and_5 (and_5_out, and_4_out, decoder_1_out0);
  and and_6 (and_6_out, and_3_out, decoder_1_out0);
  and and_7 (and_7_out, and_2_out, decoder_1_out0);
  and and_8 (and_8_out, and_1_out, decoder_1_out0);
  Hex_Digit_Display hex_digit_display_1 (.value(and_9_out));  // open: dp
  not not_2 (not_2_out, not_1_out);
  D_Flip_Flop d_ff_1 (.D(and_5_out), .clk(demultiplexer_1_out0), .Q(d_ff_1_q));  // open: Qn, preset, reset
  // NoConnect on undriven
  D_Flip_Flop d_ff_2 (.D(and_6_out), .clk(demultiplexer_1_out0), .Q(d_ff_2_q), .preset(undriven));  // open: Qn, reset
  D_Flip_Flop d_ff_3 (.D(and_7_out), .clk(demultiplexer_1_out0), .Q(d_ff_3_q), .reset(undriven_2));  // open: Qn, preset
  // NoConnect on undriven_2
  D_Flip_Flop d_ff_4 (.D(and_8_out), .clk(demultiplexer_1_out0), .Q(d_ff_4_q));  // open: Qn, preset, reset
  and and_9 (and_9_out[0], d_ff_1_q, decoder_1_out0, not_2_out);
  and and_10 (and_9_out[1], d_ff_2_q, decoder_1_out0, not_2_out);
  and and_11 (and_9_out[2], d_ff_3_q, decoder_1_out0, not_2_out);
  and and_12 (and_9_out[3], d_ff_4_q, decoder_1_out0, not_2_out);
  and and_13 (and_13_out, not_1_out, dipswitch_2_p1);
  and and_14 (and_14_out, not_1_out, dipswitch_1_p3);
  and and_15 (and_15_out, not_1_out, dipswitch_1_p2);
  and and_16 (and_16_out, not_1_out, dipswitch_1_p1);
  D_Flip_Flop d_ff_5 (.D(and_17_out), .clk(demultiplexer_1_out1), .Q(d_ff_5_q));  // open: Qn, preset, reset
  and and_17 (and_17_out, and_16_out, decoder_1_out1);
  D_Flip_Flop d_ff_6 (
    .D(and_18_out), .clk(demultiplexer_1_out1), .Q(d_ff_6_q), .preset(undriven_3));  // open: Qn, reset
  and and_18 (and_18_out, and_15_out, decoder_1_out1);
  D_Flip_Flop d_ff_7 (
    .D(and_19_out), .clk(demultiplexer_1_out1), .Q(d_ff_7_q), .reset(undriven_4));  // open: Qn, preset
  and and_19 (and_19_out, and_14_out, decoder_1_out1);
  D_Flip_Flop d_ff_8 (.D(and_20_out), .clk(demultiplexer_1_out1), .Q(d_ff_8_q));  // open: Qn, preset, reset
  and and_20 (and_20_out, and_13_out, decoder_1_out1);
  Hex_Digit_Display hex_digit_display_2 (.value(and_9_out));  // open: dp
  // NoConnect on undriven_3
  // NoConnect on undriven_4
  and and_21 (and_9_out[0], d_ff_5_q, decoder_1_out1, not_3_out);
  not not_3 (not_3_out, not_1_out);
  and and_22 (and_9_out[1], d_ff_6_q, decoder_1_out1, not_3_out);
  and and_23 (and_9_out[2], d_ff_7_q, decoder_1_out1, not_3_out);
  and and_24 (and_9_out[3], d_ff_8_q, decoder_1_out1, not_3_out);
  and and_25 (and_25_out, dipswitch_2_p1, not_1_out);
  and and_26 (and_26_out, dipswitch_1_p3, not_1_out);
  and and_27 (and_27_out, dipswitch_1_p2, not_1_out);
  and and_28 (and_28_out, dipswitch_1_p1, not_1_out);
  and and_29 (and_29_out, and_28_out, decoder_1_out2);
  and and_30 (and_30_out, and_27_out, decoder_1_out2);
  and and_31 (and_31_out, and_26_out, decoder_1_out2);
  and and_32 (and_32_out, and_25_out, decoder_1_out2);
  Hex_Digit_Display hex_digit_display_3 (.value(and_9_out));  // open: dp
  D_Flip_Flop d_ff_9 (.D(and_29_out), .clk(demultiplexer_1_out2), .Q(d_ff_9_q));  // open: Qn, preset, reset
  // NoConnect on undriven_5
  D_Flip_Flop d_ff_10 (
    .D(and_30_out), .clk(demultiplexer_1_out2), .Q(d_ff_10_q), .preset(undriven_5));  // open: Qn, reset
  D_Flip_Flop d_ff_11 (
    .D(and_31_out), .clk(demultiplexer_1_out2), .Q(d_ff_11_q), .reset(undriven_6));  // open: Qn, preset
  // NoConnect on undriven_6
  D_Flip_Flop d_ff_12 (.D(and_32_out), .clk(demultiplexer_1_out2), .Q(d_ff_12_q));  // open: Qn, preset, reset
  and and_33 (and_9_out[0], d_ff_9_q, decoder_1_out2, not_4_out);
  and and_34 (and_9_out[1], d_ff_10_q, decoder_1_out2, not_4_out);
  not not_4 (not_4_out, not_1_out);
  and and_35 (and_9_out[2], d_ff_11_q, decoder_1_out2, not_4_out);
  and and_36 (and_9_out[3], d_ff_12_q, decoder_1_out2, not_4_out);
  and and_37 (and_37_out, dipswitch_2_p1, not_1_out);
  and and_38 (and_38_out, dipswitch_1_p3, not_1_out);
  and and_39 (and_39_out, dipswitch_1_p2, not_1_out);
  and and_40 (and_40_out, dipswitch_1_p1, not_1_out);
  and and_41 (and_41_out, and_40_out, decoder_1_out3);
  and and_42 (and_42_out, and_39_out, decoder_1_out3);
  and and_43 (and_43_out, and_38_out, decoder_1_out3);
  and and_44 (and_44_out, and_37_out, decoder_1_out3);
  Hex_Digit_Display hex_digit_display_4 (.value(and_9_out));  // open: dp
  D_Flip_Flop d_ff_13 (.D(and_41_out), .clk(demultiplexer_1_out3), .Q(d_ff_13_q));  // open: Qn, preset, reset
  // NoConnect on undriven_7
  D_Flip_Flop d_ff_14 (
    .D(and_42_out), .clk(demultiplexer_1_out3), .Q(d_ff_14_q), .preset(undriven_7));  // open: Qn, reset
  D_Flip_Flop d_ff_15 (
    .D(and_43_out), .clk(demultiplexer_1_out3), .Q(d_ff_15_q), .reset(undriven_8));  // open: Qn, preset
  // NoConnect on undriven_8
  D_Flip_Flop d_ff_16 (.D(and_44_out), .clk(demultiplexer_1_out3), .Q(d_ff_16_q));  // open: Qn, preset, reset
  and and_45 (and_9_out[0], d_ff_13_q, decoder_1_out3, not_5_out);
  and and_46 (and_9_out[1], d_ff_14_q, decoder_1_out3, not_5_out);
  not not_5 (not_5_out, not_1_out);
  and and_47 (and_9_out[2], d_ff_15_q, decoder_1_out3, not_5_out);
  and and_48 (and_9_out[3], d_ff_16_q, decoder_1_out3, not_5_out);
  Hex_Digit_Display hex_digit_display_5 (.value(and_9_out));  // open: dp

  // Notes on the sheet:
  //   main bus
  //   THIRD IS CHIP ENABLE
  //   FOURTH IS READ/WRITE
  //   FIRST TWO BITS OF SELECTION OF REGISTER
endmodule
