// Logisim project NewCPU.circ as structural Verilog: 9 circuits, main circuit main
module main (
);

  wire clock_1_out, clock_2_out, clock_3_out, clock_4_out, CLR, control_1_alu_en, control_1_load_a,
       control_1_load_b, control_1_mov_ab, control_1_mov_ba, control_1_sub, dipswitch_2_p1, n74157_1_pin4,
       n74157_1_pin7, n74157_1_pin9, n74157_1_pin12;
  wire [2:0] control_1_alu_op, instruction_reg_1_op;
  wire [3:0] ALU_RESULT, InstructionIMM, MUX2OUT, n74157_3_pin4, program_counter_1_countout, Red_A_Q, Red_B_Q;
  wire [7:0] ram_simulator_1_d_out, undriven;

  DipSwitch dipswitch_1 (.sw2(CLR));  // open: sw1, sw3, sw4, sw5, sw6, sw7, sw8
  Clock clock_1 (.out(clock_1_out));
  // DipSwitch dipswitch_2: pin names not known; wires that end beside it: dipswitch_2_p1, dipswitch_2_p1
  Program_counter program_counter_1 (.nCLR(CLR), .Clock(clock_1_out), .CountOut(program_counter_1_countout));
  Clock clock_2 (.out(clock_2_out));
  RAM_Simulator ram_simulator_1 (.Addr(program_counter_1_countout), .D_IN(undriven), .D_OUT(ram_simulator_1_d_out));
  instruction_reg instruction_reg_1 (
    .IR_IN(ram_simulator_1_d_out), .nCLR(CLR), .CLK(clock_2_out), .IMM(InstructionIMM),
    .OP(instruction_reg_1_op));
  control control_1 (
    .OP(instruction_reg_1_op), .LOAD_A(control_1_load_a), .LOAD_B(control_1_load_b),
    .MOV_AB(control_1_mov_ab), .MOV_BA(control_1_mov_ba), .SUB(control_1_sub), .ALU_EN(control_1_alu_en),
    .ALU_OP(control_1_alu_op));  // open: DO_ADD, DO_SUB, DO_AND, DO_OR
  Hex_Digit_Display hex_digit_display_1 (.value(InstructionIMM));  // open: dp
  _74157 #(.ShowInternalStructure("true")) u_74157_1 (
    .pin1(control_1_alu_en), .pin2(InstructionIMM[0]), .pin3(ALU_RESULT[0]), .pin4(n74157_1_pin4),
    .pin5(InstructionIMM[1]), .pin6(ALU_RESULT[1]), .pin7(n74157_1_pin7), .pin14(InstructionIMM[3]),
    .pin13(ALU_RESULT[3]), .pin12(n74157_1_pin12), .pin11(InstructionIMM[2]), .pin10(ALU_RESULT[2]),
    .pin9(n74157_1_pin9));  // open: pin15
  _74157 #(.ShowInternalStructure("true")) u_74157_2 (
    .pin1(control_1_mov_ba), .pin2(n74157_1_pin4), .pin3(Red_B_Q[0]), .pin4(MUX2OUT[0]),
    .pin5(n74157_1_pin7), .pin6(Red_B_Q[1]), .pin7(MUX2OUT[1]), .pin14(n74157_1_pin12), .pin13(Red_B_Q[3]),
    .pin12(MUX2OUT[3]), .pin11(n74157_1_pin9), .pin10(Red_B_Q[2]), .pin9(MUX2OUT[2]));  // open: pin15
  _74157 #(.ShowInternalStructure("true")) u_74157_3 (
    .pin1(control_1_mov_ab), .pin2(InstructionIMM[0]), .pin3(Red_A_Q[0]), .pin4(n74157_3_pin4[0]),
    .pin5(InstructionIMM[1]), .pin6(Red_A_Q[1]), .pin7(n74157_3_pin4[1]), .pin14(InstructionIMM[3]),
    .pin13(Red_A_Q[3]), .pin12(n74157_3_pin4[3]), .pin11(InstructionIMM[2]), .pin10(Red_A_Q[2]),
    .pin9(n74157_3_pin4[2]));  // open: pin15
  Hex_Digit_Display hex_digit_display_2 (.value(ALU_RESULT));  // open: dp
  alu alu_1 (.A(Red_A_Q), .B(Red_B_Q), .SUB(control_1_sub), .OP(control_1_alu_op), .RESULT(ALU_RESULT));
  Clock clock_3 (.out(clock_3_out));
  Clock clock_4 (.out(clock_4_out));
  reg_a reg_a_1 (.nCLR(CLR), .D(MUX2OUT), .LOAD(control_1_load_a), .CLK(clock_3_out), .Q(Red_A_Q));
  Hex_Digit_Display hex_digit_display_3 (.value(Red_A_Q));  // open: dp
  Hex_Digit_Display hex_digit_display_4 (.value(Red_B_Q));  // open: dp
  reg_b reg_b_1 (.nCLR(CLR), .D(n74157_3_pin4), .LOAD(control_1_load_b), .CLK(clock_4_out), .Q(Red_B_Q));
endmodule

module full_adder_1_bit (
  input  A,
  input  B,
  input  CIN,
  output SUM,
  output COUT
);

  wire n7408_1_pin3, n7408_1_pin11, n7486_1_pin6;

  _7486 #(.ShowInternalStructure("true")) u_7486_1 (
    .pin4(A), .pin5(B), .pin6(n7486_1_pin6), .pin10(n7486_1_pin6), .pin9(CIN), .pin8(SUM));  // open: pin1, pin2, pin3, pin13, pin12, pin11
  _7408 #(.ShowInternalStructure("true")) u_7408_1 (
    .pin1(A), .pin2(B), .pin3(n7408_1_pin3), .pin13(n7486_1_pin6), .pin12(CIN), .pin11(n7408_1_pin11));  // open: pin4, pin5, pin6, pin10, pin9, pin8
  _7432 #(.ShowInternalStructure("true")) u_7432_1 (
    .pin13(n7408_1_pin11), .pin12(n7408_1_pin3), .pin11(COUT));  // open: pin1, pin2, pin3, pin4, pin5, pin6, pin10, pin9, pin8
  // _74181 74181_1: pin names not known
endmodule

module Program_counter (
  input  nCLR,
  input  Clock,
  output [3:0] CountOut
);

  wire n74161_1_pin3, n74161_1_pin7;

  _74161 #(.ShowInternalStructure("true")) u_74161_1 (
    .pin1(nCLR), .pin2(Clock), .pin3(n74161_1_pin3), .pin4(n74161_1_pin3), .pin5(n74161_1_pin3),
    .pin6(n74161_1_pin3), .pin7(n74161_1_pin7), .pin14(CountOut[0]), .pin13(CountOut[1]),
    .pin12(CountOut[2]), .pin11(CountOut[3]), .pin10(n74161_1_pin7), .pin9(n74161_1_pin7));  // open: pin15
  // also tied to GND on the sheet: n74161_1_pin3
  // also tied to VCC on the sheet: n74161_1_pin7
endmodule

module RAM_Simulator (
  input  [3:0] Addr,
  input  [7:0] D_IN,
  output [7:0] D_OUT
);


  assign D_OUT = D_IN;
endmodule

module instruction_reg (
  input  [7:0] IR_IN,
  input  nCLR,
  input  CLK,
  output [3:0] IMM,
  output [2:0] OP
);

  wire n74175_2_pin2;
  wire [0:0] pull_resistor_1_node;

  Pull_Resistor pull_resistor_1 (.node(pull_resistor_1_node[0]));
  _74175 #(.ShowInternalStructure("true")) u_74175_1 (
    .pin1(nCLR), .pin2(IMM[3]), .pin4(IR_IN[3]), .pin5(IR_IN[2]), .pin7(IMM[2]), .pin15(IMM[0]),
    .pin13(IR_IN[0]), .pin12(IR_IN[1]), .pin10(IMM[1]), .pin9(CLK));  // open: pin3, pin6, pin14, pin11
  _74175 u_74175_2 (
    .pin1(nCLR), .pin2(n74175_2_pin2), .pin4(pull_resistor_1_node[0]), .pin5(IR_IN[6]), .pin7(OP[2]),
    .pin15(OP[0]), .pin13(IR_IN[4]), .pin12(IR_IN[5]), .pin10(OP[1]), .pin9(CLK));  // open: pin3, pin6, pin14, pin11
endmodule

module reg_a (
  input  nCLR,
  input  [3:0] D,
  input  LOAD,
  input  CLK,
  output [3:0] Q
);

  wire n74175_1_pin9;

  _74175 #(.ShowInternalStructure("true")) u_74175_1 (
    .pin1(nCLR), .pin2(Q[0]), .pin4(D[0]), .pin5(D[1]), .pin7(Q[1]), .pin15(Q[3]), .pin13(D[3]),
    .pin12(D[2]), .pin10(Q[2]), .pin9(n74175_1_pin9));  // open: pin3, pin6, pin14, pin11
  _7408 #(.ShowInternalStructure("true")) u_7408_1 (
    .pin1(LOAD), .pin2(CLK), .pin3(n74175_1_pin9));  // open: pin4, pin5, pin6, pin13, pin12, pin11, pin10, pin9, pin8
endmodule

module reg_b (
  input  nCLR,
  input  [3:0] D,
  input  LOAD,
  input  CLK,
  output [3:0] Q
);

  wire n74175_1_pin9;

  _74175 #(.ShowInternalStructure("true")) u_74175_1 (
    .pin1(nCLR), .pin2(Q[0]), .pin4(D[0]), .pin5(D[1]), .pin7(Q[1]), .pin15(Q[3]), .pin13(D[3]),
    .pin12(D[2]), .pin10(Q[2]), .pin9(n74175_1_pin9));  // open: pin3, pin6, pin14, pin11
  _7408 #(.ShowInternalStructure("true")) u_7408_1 (
    .pin1(LOAD), .pin2(CLK), .pin3(n74175_1_pin9));  // open: pin4, pin5, pin6, pin13, pin12, pin11, pin10, pin9, pin8
endmodule

module alu (
  input  [3:0] A,
  input  [3:0] B,
  input  SUB,
  input  [2:0] OP,
  output [3:0] RESULT
);

  wire AndSig, full_adder_1_bit_1_cout, full_adder_1_bit_2_cout, full_adder_1_bit_3_cout, n7419_1_pin3,
       n7419_1_pin4, n7419_1_pin5, n7419_1_pin9, n7419_1_pin10, n7419_1_pin11, n7419_1_pin12, n7486_1_pin3,
       n7486_1_pin6, n7486_1_pin8, n7486_1_pin11, n74157_1_pin4, n74157_1_pin7, n74157_1_pin9,
       n74157_1_pin12, OrSig;
  wire [3:0] AndOut, OROut, SumOut;

  _7419 #(.ShowInternalStructure("true")) u_7419_1 (
    .pin3(n7419_1_pin3), .pin4(n7419_1_pin4), .pin5(n7419_1_pin5), .pin6(OrSig), .pin13(OP[2]),
    .pin12(n7419_1_pin12), .pin11(n7419_1_pin11), .pin10(n7419_1_pin10), .pin9(n7419_1_pin9), .pin8(AndSig));  // open: pin1, pin2
  _7486 #(.ShowInternalStructure("true")) u_7486_1 (
    .pin1(B[0]), .pin2(n7419_1_pin4), .pin3(n7486_1_pin3), .pin4(B[1]), .pin5(n7419_1_pin4),
    .pin6(n7486_1_pin6), .pin13(B[2]), .pin12(n7419_1_pin4), .pin11(n7486_1_pin11), .pin10(B[3]),
    .pin9(n7419_1_pin4), .pin8(n7486_1_pin8));
  _74139 #(.ShowInternalStructure("true")) u_74139_1 (
    .pin1(n7419_1_pin12), .pin2(OP[1]), .pin3(OP[0]), .pin4(n7419_1_pin11), .pin5(n7419_1_pin9),
    .pin6(n7419_1_pin3), .pin7(n7419_1_pin5));  // open: pin15, pin14, pin13, pin12, pin11, pin10, pin9
  _7408 u_7408_1 (
    .pin1(A[0]), .pin2(B[0]), .pin3(AndOut[0]), .pin4(A[1]), .pin5(B[1]), .pin6(AndOut[1]), .pin13(A[2]),
    .pin12(B[2]), .pin11(AndOut[2]), .pin10(A[3]), .pin9(B[3]), .pin8(AndOut[3]));
  _7432 u_7432_1 (
    .pin1(A[0]), .pin2(B[0]), .pin3(OROut[0]), .pin4(A[1]), .pin5(B[1]), .pin6(OROut[1]), .pin13(A[2]),
    .pin12(B[2]), .pin11(OROut[2]), .pin10(A[3]), .pin9(B[3]), .pin8(OROut[3]));
  full_adder_1_bit full_adder_1_bit_1 (
    .A(A[0]), .B(n7486_1_pin3), .CIN(n7419_1_pin4), .SUM(SumOut[0]), .COUT(full_adder_1_bit_1_cout));
  full_adder_1_bit full_adder_1_bit_2 (
    .A(A[1]), .B(n7486_1_pin6), .CIN(full_adder_1_bit_1_cout), .SUM(SumOut[1]), .COUT(full_adder_1_bit_2_cout));
  full_adder_1_bit full_adder_1_bit_3 (
    .A(A[2]), .B(n7486_1_pin11), .CIN(full_adder_1_bit_2_cout), .SUM(SumOut[2]),
    .COUT(full_adder_1_bit_3_cout));
  full_adder_1_bit full_adder_1_bit_4 (
    .A(A[3]), .B(n7486_1_pin8), .CIN(full_adder_1_bit_3_cout), .SUM(SumOut[3]));  // open: COUT
  Hex_Digit_Display hex_digit_display_1 (.value(SumOut));  // open: dp
  _74157 #(.ShowInternalStructure("true")) u_74157_1 (
    .pin1(AndSig), .pin2(SumOut[0]), .pin3(AndOut[0]), .pin4(n74157_1_pin4), .pin5(SumOut[1]),
    .pin6(AndOut[1]), .pin7(n74157_1_pin7), .pin14(SumOut[3]), .pin13(AndOut[3]), .pin12(n74157_1_pin12),
    .pin11(SumOut[2]), .pin10(AndOut[2]), .pin9(n74157_1_pin9));  // open: pin15
  _74157 #(.ShowInternalStructure("true")) u_74157_2 (
    .pin1(OrSig), .pin2(n74157_1_pin4), .pin3(OROut[0]), .pin4(RESULT[0]), .pin5(n74157_1_pin7),
    .pin6(OROut[1]), .pin7(RESULT[1]), .pin14(n74157_1_pin12), .pin13(OROut[3]), .pin12(RESULT[3]),
    .pin11(n74157_1_pin9), .pin10(OROut[2]), .pin9(RESULT[2]));  // open: pin15
  Hex_Digit_Display hex_digit_display_2 (.value(RESULT));  // open: dp
endmodule

module control (
  input  [2:0] OP,
  output LOAD_A,
  output LOAD_B,
  output MOV_AB,
  output MOV_BA,
  output DO_ADD,
  output DO_SUB,
  output DO_AND,
  output DO_OR,
  output SUB,
  output ALU_EN,
  output [2:0] ALU_OP
);

  wire n7404_1_pin2, n7404_1_pin4, n7432_1_pin4, n7432_1_pin5, n74138_1_pin4, n74138_1_pin5, n74138_1_pin6,
       n74138_1_pin7, n74138_1_pin9, n74138_1_pin10, n74138_1_pin11, n74138_1_pin12, n74138_1_pin13,
       n74138_1_pin14, n74138_1_pin15;

  _74138 #(.ShowInternalStructure("true")) u_74138_1 (
    .pin1(OP[0]), .pin2(OP[1]), .pin3(OP[2]), .pin4(n74138_1_pin4), .pin5(n74138_1_pin5),
    .pin6(n74138_1_pin6), .pin7(n74138_1_pin7), .pin15(n74138_1_pin15), .pin14(n74138_1_pin14),
    .pin13(n74138_1_pin13), .pin12(n74138_1_pin12), .pin11(n74138_1_pin11), .pin10(n74138_1_pin10),
    .pin9(n74138_1_pin9));
  _7404 u_7404_1 (
    .pin1(n74138_1_pin15), .pin2(n7404_1_pin2), .pin3(n74138_1_pin14), .pin4(n7404_1_pin4),
    .pin5(n74138_1_pin13), .pin6(MOV_AB), .pin13(n74138_1_pin12), .pin12(MOV_BA), .pin11(n74138_1_pin11),
    .pin10(DO_ADD), .pin9(n74138_1_pin10), .pin8(DO_SUB));
  _7400 u_7400_1 (
    .pin1(n74138_1_pin9), .pin2(n74138_1_pin9), .pin3(DO_AND), .pin4(n74138_1_pin7), .pin5(n74138_1_pin7),
    .pin6(DO_OR));  // open: pin13, pin12, pin11, pin10, pin9, pin8
  _7432 u_7432_1 (
    .pin4(n7432_1_pin4), .pin5(n7432_1_pin5), .pin6(ALU_EN), .pin13(DO_ADD), .pin12(DO_SUB),
    .pin11(n7432_1_pin4), .pin10(DO_AND), .pin9(DO_OR), .pin8(n7432_1_pin5));  // open: pin1, pin2, pin3
  _7432 #(.ShowInternalStructure("true")) u_7432_2 (
    .pin1(n7404_1_pin2), .pin2(MOV_BA), .pin3(LOAD_A), .pin4(n7404_1_pin4), .pin5(MOV_AB), .pin6(LOAD_B));  // open: pin13, pin12, pin11, pin10, pin9, pin8

  assign ALU_OP = OP;
  assign SUB = DO_SUB;
  // also tied to GND on the sheet: {n74138_1_pin4, n74138_1_pin5}
  // also tied to VCC on the sheet: n74138_1_pin6
endmodule
