// Logisim project PleaseWork.circ as structural Verilog: 1 circuit, main circuit main
module main (
);

  wire dipswitch_1_p1, dipswitch_1_p2, dipswitch_1_p3, dipswitch_1_p4, n74175_1_pin1, n74175_1_pin9,
       n74175_2_pin1, n74175_2_pin9, n74241_1_pin2, n74241_1_pin3, n74241_1_pin4, n74241_1_pin5,
       n74241_1_pin6, n74241_1_pin7, n74241_1_pin8, n74241_1_pin9, n74241_2_pin2, n74241_2_pin3,
       n74241_2_pin4, n74241_2_pin5, n74241_2_pin6, n74241_2_pin7, n74241_2_pin8, n74241_2_pin9,
       n74283_1_pin1, n74283_1_pin4, n74283_1_pin10, n74283_1_pin13;
  wire [3:0] controlled_buffer_4_out;

  // DipSwitch dipswitch_1: pin names not known; wires that end beside it: dipswitch_1_p1, dipswitch_1_p2, dipswitch_1_p3, dipswitch_1_p4
  Controlled_Buffer controlled_buffer_1 (.out(controlled_buffer_4_out[3]), .en(dipswitch_1_p4));  // open: in
  Controlled_Buffer controlled_buffer_2 (.out(controlled_buffer_4_out[2]), .en(dipswitch_1_p4));  // open: in
  Controlled_Buffer controlled_buffer_3 (.out(controlled_buffer_4_out[1]), .en(dipswitch_1_p4));  // open: in
  Controlled_Buffer controlled_buffer_4 (.out(controlled_buffer_4_out[0]), .en(dipswitch_1_p4));  // open: in
  Pull_Resistor pull_resistor_1 (.node(controlled_buffer_4_out[3]));
  Pull_Resistor pull_resistor_2 (.node(controlled_buffer_4_out[2]));
  Pull_Resistor pull_resistor_3 (.node(controlled_buffer_4_out[1]));
  Pull_Resistor pull_resistor_4 (.node(controlled_buffer_4_out[0]));
  _74241 #(.ShowInternalStructure("true")) u_74241_1 (
    .pin1(dipswitch_1_p1), .pin2(n74241_1_pin2), .pin3(n74241_1_pin3), .pin4(n74241_1_pin4),
    .pin5(n74241_1_pin5), .pin6(n74241_1_pin6), .pin7(n74241_1_pin7), .pin8(n74241_1_pin8),
    .pin9(n74241_1_pin9), .pin19(dipswitch_1_p1), .pin18(controlled_buffer_4_out[0]),
    .pin17(controlled_buffer_4_out[0]), .pin16(controlled_buffer_4_out[1]),
    .pin15(controlled_buffer_4_out[1]), .pin14(controlled_buffer_4_out[2]),
    .pin13(controlled_buffer_4_out[2]), .pin12(controlled_buffer_4_out[3]), .pin11(controlled_buffer_4_out[3]));
  _74175 u_74175_1 (
    .pin1(n74175_1_pin1), .pin2(n74241_1_pin2), .pin4(n74241_1_pin3), .pin5(n74241_1_pin5),
    .pin7(n74241_1_pin4), .pin15(n74241_1_pin6), .pin13(n74241_1_pin7), .pin12(n74241_1_pin9),
    .pin10(n74241_1_pin8), .pin9(n74175_1_pin9));  // open: pin3, pin6, pin14, pin11
  _74241 #(.ShowInternalStructure("true")) u_74241_2 (
    .pin1(dipswitch_1_p2), .pin2(n74241_2_pin2), .pin3(n74241_2_pin3), .pin4(n74241_2_pin4),
    .pin5(n74241_2_pin5), .pin6(n74241_2_pin6), .pin7(n74241_2_pin7), .pin8(n74241_2_pin8),
    .pin9(n74241_2_pin9), .pin19(dipswitch_1_p2), .pin18(controlled_buffer_4_out[0]),
    .pin17(controlled_buffer_4_out[0]), .pin16(controlled_buffer_4_out[1]),
    .pin15(controlled_buffer_4_out[1]), .pin14(controlled_buffer_4_out[2]),
    .pin13(controlled_buffer_4_out[2]), .pin12(controlled_buffer_4_out[3]), .pin11(controlled_buffer_4_out[3]));
  _74175 u_74175_2 (
    .pin1(n74175_2_pin1), .pin2(n74241_2_pin2), .pin4(n74241_2_pin3), .pin5(n74241_2_pin5),
    .pin7(n74241_2_pin4), .pin15(n74241_2_pin6), .pin13(n74241_2_pin7), .pin12(n74241_2_pin9),
    .pin10(n74241_2_pin8), .pin9(n74175_2_pin9));  // open: pin3, pin6, pin14, pin11
  Hex_Digit_Display hex_digit_display_1 (.value(controlled_buffer_4_out));  // open: dp
  _74283 #(.ShowInternalStructure("true")) u_74283_1 (
    .pin1(n74283_1_pin1), .pin2(n74241_2_pin4), .pin3(controlled_buffer_4_out[1]), .pin4(n74283_1_pin4),
    .pin5(controlled_buffer_4_out[0]), .pin6(n74241_2_pin2), .pin15(n74241_2_pin6),
    .pin14(controlled_buffer_4_out[2]), .pin13(n74283_1_pin13), .pin12(controlled_buffer_4_out[3]),
    .pin11(n74241_2_pin8), .pin10(n74283_1_pin10));  // open: pin7, pin9
  _74241 #(.ShowInternalStructure("true")) u_74241_3 (
    .pin1(dipswitch_1_p3), .pin3(controlled_buffer_4_out[3]), .pin5(controlled_buffer_4_out[2]),
    .pin7(controlled_buffer_4_out[1]), .pin9(controlled_buffer_4_out[0]), .pin19(dipswitch_1_p3),
    .pin17(n74283_1_pin10), .pin15(n74283_1_pin13), .pin13(n74283_1_pin1), .pin11(n74283_1_pin4));  // open: pin2, pin4, pin6, pin8, pin18, pin16, pin14, pin12
  // also tied to VCC on the sheet: {n74175_1_pin1, n74175_2_pin1}
endmodule
