// Logisim project Register.circ as structural Verilog: 1 circuit, main circuit main
module main (
);

  wire and_1_out, and_2_out, and_3_out, and_4_out, and_5_out, and_6_out, and_7_out, and_8_out, and_9_out,
       and_14_out, and_15_out, and_16_out, and_17_out, and_18_out, and_19_out, and_20_out, and_21_out,
       and_26_out, and_27_out, and_28_out, and_29_out, and_30_out, and_31_out, and_32_out, and_33_out,
       and_38_out, and_39_out, and_40_out, and_41_out, and_42_out, and_43_out, and_44_out, and_45_out,
       button_1_out, d_ff_1_q, d_ff_2_q, d_ff_3_q, d_ff_4_q, d_ff_5_q, d_ff_6_q, d_ff_7_q, d_ff_8_q,
       d_ff_9_q, d_ff_10_q, d_ff_11_q, d_ff_12_q, d_ff_13_q, d_ff_14_q, d_ff_15_q, d_ff_16_q, decoder_1_out0,
       decoder_1_out1, decoder_1_out2, decoder_1_out3, demultiplexer_1_out0, demultiplexer_1_out1,
       demultiplexer_1_out2, demultiplexer_1_out3, dipswitch_2_p4, dipswitch_2_p5, not_1_out, not_2_out,
       not_3_out, not_4_out, not_5_out, not_6_out, undriven, undriven_2, undriven_3, undriven_4, undriven_5,
       undriven_6, undriven_7, undriven_8;
  wire [1:0] dipswitch_2_p3;
  wire [3:0] and_10_out, and_22_out, and_34_out, and_46_out, controlled_buffer_1_out,
       controlled_buffer_13_out, dipswitch_1_p1;

  Button button_1 (.out(button_1_out));
  // DipSwitch #(.number(4)) dipswitch_1: pin names not known; wires that end beside it: dipswitch_1_p1[0], dipswitch_1_p1[1], dipswitch_1_p1[2]
  // DipSwitch #(.number(4)) dipswitch_2: pin names not known; wires that end beside it: dipswitch_1_p1[3], dipswitch_2_p3[1], dipswitch_2_p3[0], dipswitch_2_p4, dipswitch_2_p5
  not not_1 (not_1_out, dipswitch_2_p5);
  Hex_Digit_Display hex_digit_display_1 (.value(controlled_buffer_13_out));  // open: dp
  and and_1 (and_1_out, not_1_out, button_1_out);
  Decoder #(.select(2)) decoder_1 (
    .out0(decoder_1_out0), .out1(decoder_1_out1), .out2(decoder_1_out2), .out3(decoder_1_out3),
    .sel(dipswitch_2_p3), .en(dipswitch_2_p4));
  Demultiplexer #(.select(2)) demultiplexer_1 (
    .out0(demultiplexer_1_out0), .out1(demultiplexer_1_out1), .out2(demultiplexer_1_out2),
    .out3(demultiplexer_1_out3), .in(and_1_out), .sel(dipswitch_2_p3));
  and and_2 (and_2_out, not_1_out, dipswitch_1_p1[3]);
  and and_3 (and_3_out, not_1_out, dipswitch_1_p1[2]);
  and and_4 (and_4_out, not_1_out, dipswitch_1_p1[1]);
  and and_5 (and_5_out, not_1_out, dipswitch_1_p1[0]);
  and and_6 (and_6_out, and_5_out, decoder_1_out0);
  and and_7 (and_7_out, and_4_out, decoder_1_out0);
  and and_8 (and_8_out, and_3_out, decoder_1_out0);
  and and_9 (and_9_out, and_2_out, decoder_1_out0);
  Hex_Digit_Display hex_digit_display_2 (.value(and_10_out));  // open: dp
  not not_2 (not_2_out, not_1_out);
  D_Flip_Flop d_ff_1 (.D(and_6_out), .clk(demultiplexer_1_out0), .Q(d_ff_1_q));  // open: Qn, preset, reset
  // NoConnect on undriven
  D_Flip_Flop d_ff_2 (.D(and_7_out), .clk(demultiplexer_1_out0), .Q(d_ff_2_q), .preset(undriven));  // open: Qn, reset
  D_Flip_Flop d_ff_3 (.D(and_8_out), .clk(demultiplexer_1_out0), .Q(d_ff_3_q), .reset(undriven_2));  // open: Qn, preset
  // NoConnect on undriven_2
  D_Flip_Flop d_ff_4 (.D(and_9_out), .clk(demultiplexer_1_out0), .Q(d_ff_4_q));  // open: Qn, preset, reset
  and and_10 (and_10_out[0], d_ff_1_q, decoder_1_out0, not_2_out);
  and and_11 (and_10_out[1], d_ff_2_q, decoder_1_out0, not_2_out);
  and and_12 (and_10_out[2], d_ff_3_q, decoder_1_out0, not_2_out);
  and and_13 (and_10_out[3], d_ff_4_q, decoder_1_out0, not_2_out);
  and and_14 (and_14_out, not_1_out, dipswitch_1_p1[3]);
  and and_15 (and_15_out, not_1_out, dipswitch_1_p1[2]);
  assign controlled_buffer_1_out[0] = decoder_1_out0 ? and_10_out[0] : 1'bz;  // Controlled_Buffer controlled_buffer_1
  assign controlled_buffer_1_out[1] = decoder_1_out0 ? and_10_out[1] : 1'bz;  // Controlled_Buffer controlled_buffer_2
  assign controlled_buffer_1_out[2] = decoder_1_out0 ? and_10_out[2] : 1'bz;  // Controlled_Buffer controlled_buffer_3
  assign controlled_buffer_1_out[3] = decoder_1_out0 ? and_10_out[3] : 1'bz;  // Controlled_Buffer controlled_buffer_4
  and and_16 (and_16_out, not_1_out, dipswitch_1_p1[1]);
  and and_17 (and_17_out, not_1_out, dipswitch_1_p1[0]);
  D_Flip_Flop d_ff_5 (.D(and_18_out), .clk(demultiplexer_1_out1), .Q(d_ff_5_q));  // open: Qn, preset, reset
  and and_18 (and_18_out, and_17_out, decoder_1_out1);
  D_Flip_Flop d_ff_6 (
    .D(and_19_out), .clk(demultiplexer_1_out1), .Q(d_ff_6_q), .preset(undriven_3));  // open: Qn, reset
  and and_19 (and_19_out, and_16_out, decoder_1_out1);
  D_Flip_Flop d_ff_7 (
    .D(and_20_out), .clk(demultiplexer_1_out1), .Q(d_ff_7_q), .reset(undriven_4));  // open: Qn, preset
  and and_20 (and_20_out, and_15_out, decoder_1_out1);
  D_Flip_Flop d_ff_8 (.D(and_21_out), .clk(demultiplexer_1_out1), .Q(d_ff_8_q));  // open: Qn, preset, reset
  and and_21 (and_21_out, and_14_out, decoder_1_out1);
  Hex_Digit_Display hex_digit_display_3 (.value(and_22_out));  // open: dp
  // NoConnect on undriven_3
  // NoConnect on undriven_4
  and and_22 (and_22_out[0], d_ff_5_q, decoder_1_out1, not_3_out);
  assign controlled_buffer_1_out[0] = decoder_1_out1 ? and_22_out[0] : 1'bz;  // Controlled_Buffer controlled_buffer_5
  not not_3 (not_3_out, not_1_out);
  and and_23 (and_22_out[1], d_ff_6_q, decoder_1_out1, not_3_out);
  and and_24 (and_22_out[2], d_ff_7_q, decoder_1_out1, not_3_out);
  and and_25 (and_22_out[3], d_ff_8_q, decoder_1_out1, not_3_out);
  assign controlled_buffer_1_out[1] = decoder_1_out1 ? and_22_out[1] : 1'bz;  // Controlled_Buffer controlled_buffer_6
  assign controlled_buffer_1_out[2] = decoder_1_out1 ? and_22_out[2] : 1'bz;  // Controlled_Buffer controlled_buffer_7
  assign controlled_buffer_1_out[3] = decoder_1_out1 ? and_22_out[3] : 1'bz;  // Controlled_Buffer controlled_buffer_8
  and and_26 (and_26_out, dipswitch_1_p1[3], not_1_out);
  and and_27 (and_27_out, dipswitch_1_p1[2], not_1_out);
  and and_28 (and_28_out, dipswitch_1_p1[1], not_1_out);
  and and_29 (and_29_out, dipswitch_1_p1[0], not_1_out);
  and and_30 (and_30_out, and_29_out, decoder_1_out2);
  and and_31 (and_31_out, and_28_out, decoder_1_out2);
  and and_32 (and_32_out, and_27_out, decoder_1_out2);
  and and_33 (and_33_out, and_26_out, decoder_1_out2);
  Hex_Digit_Display hex_digit_display_4 (.value(and_34_out));  // open: dp
  D_Flip_Flop d_ff_9 (.D(and_30_out), .clk(demultiplexer_1_out2), .Q(d_ff_9_q));  // open: Qn, preset, reset
  // NoConnect on undriven_5
  D_Flip_Flop d_ff_10 (
    .D(and_31_out), .clk(demultiplexer_1_out2), .Q(d_ff_10_q), .preset(undriven_5));  // open: Qn, reset
  D_Flip_Flop d_ff_11 (
    .D(and_32_out), .clk(demultiplexer_1_out2), .Q(d_ff_11_q), .reset(undriven_6));  // open: Qn, preset
  // NoConnect on undriven_6
  D_Flip_Flop d_ff_12 (.D(and_33_out), .clk(demultiplexer_1_out2), .Q(d_ff_12_q));  // open: Qn, preset, reset
  and and_34 (and_34_out[0], d_ff_9_q, decoder_1_out2, not_4_out);
  and and_35 (and_34_out[1], d_ff_10_q, decoder_1_out2, not_4_out);
  assign controlled_buffer_1_out[0] = decoder_1_out2 ? and_34_out[0] : 1'bz;  // Controlled_Buffer controlled_buffer_9
  assign controlled_buffer_1_out[1] = decoder_1_out2 ? and_34_out[1] : 1'bz;  // Controlled_Buffer controlled_buffer_10
  not not_4 (not_4_out, not_1_out);
  and and_36 (and_34_out[2], d_ff_11_q, decoder_1_out2, not_4_out);
  and and_37 (and_34_out[3], d_ff_12_q, decoder_1_out2, not_4_out);
  assign controlled_buffer_1_out[2] = decoder_1_out2 ? and_34_out[2] : 1'bz;  // Controlled_Buffer controlled_buffer_11
  assign controlled_buffer_1_out[3] = decoder_1_out2 ? and_34_out[3] : 1'bz;  // Controlled_Buffer controlled_buffer_12
  and and_38 (and_38_out, dipswitch_1_p1[3], not_1_out);
  assign controlled_buffer_13_out = not_1_out ? dipswitch_1_p1 : 4'bz;  // Controlled_Buffer controlled_buffer_13
  and and_39 (and_39_out, dipswitch_1_p1[2], not_1_out);
  and and_40 (and_40_out, dipswitch_1_p1[1], not_1_out);
  not not_5 (not_5_out, not_1_out);
  assign controlled_buffer_13_out = not_5_out ? controlled_buffer_1_out : 4'bz;  // Controlled_Buffer controlled_buffer_14
  and and_41 (and_41_out, dipswitch_1_p1[0], not_1_out);
  and and_42 (and_42_out, and_41_out, decoder_1_out3);
  and and_43 (and_43_out, and_40_out, decoder_1_out3);
  and and_44 (and_44_out, and_39_out, decoder_1_out3);
  and and_45 (and_45_out, and_38_out, decoder_1_out3);
  Hex_Digit_Display hex_digit_display_5 (.value(and_46_out));  // open: dp
  D_Flip_Flop d_ff_13 (.D(and_42_out), .clk(demultiplexer_1_out3), .Q(d_ff_13_q));  // open: Qn, preset, reset
  // NoConnect on undriven_7
  D_Flip_Flop d_ff_14 (
    .D(and_43_out), .clk(demultiplexer_1_out3), .Q(d_ff_14_q), .preset(undriven_7));  // open: Qn, reset
  D_Flip_Flop d_ff_15 (
    .D(and_44_out), .clk(demultiplexer_1_out3), .Q(d_ff_15_q), .reset(undriven_8));  // open: Qn, preset
  // NoConnect on undriven_8
  D_Flip_Flop d_ff_16 (.D(and_45_out), .clk(demultiplexer_1_out3), .Q(d_ff_16_q));  // open: Qn, preset, reset
  and and_46 (and_46_out[0], d_ff_13_q, decoder_1_out3, not_6_out);
  and and_47 (and_46_out[1], d_ff_14_q, decoder_1_out3, not_6_out);
  assign controlled_buffer_1_out[0] = decoder_1_out3 ? and_46_out[0] : 1'bz;  // Controlled_Buffer controlled_buffer_15
  assign controlled_buffer_1_out[1] = decoder_1_out3 ? and_46_out[1] : 1'bz;  // Controlled_Buffer controlled_buffer_16
  not not_6 (not_6_out, not_1_out);
  and and_48 (and_46_out[2], d_ff_15_q, decoder_1_out3, not_6_out);
  and and_49 (and_46_out[3], d_ff_16_q, decoder_1_out3, not_6_out);
  assign controlled_buffer_1_out[2] = decoder_1_out3 ? and_46_out[2] : 1'bz;  // Controlled_Buffer controlled_buffer_17
  assign controlled_buffer_1_out[3] = decoder_1_out3 ? and_46_out[3] : 1'bz;  // Controlled_Buffer controlled_buffer_18
  Hex_Digit_Display hex_digit_display_6 (.value(controlled_buffer_1_out));  // open: dp
  Hex_Digit_Display hex_digit_display_7 (.value(controlled_buffer_13_out));  // open: dp

  // Notes on the sheet:
  //   CEN when 1
  //   First two bits are 2 bit binary index for a register 
  //   Last is read/write with read at 0 and write at 1
  //   Input Bus
  //   Output bus
  //   Main read/write common bus
endmodule
