// Logisim project RegisterRamCU.circ as structural Verilog: 1 circuit, main circuit main
module main (
);

  wire buffer_1_out, buffer_2_out, buffer_3_out, buffer_4_out, buffer_5_out, button_1_out,
       controlled_buffer_1_out, controlled_buffer_4_out, controlled_buffer_5_out, controlled_inverter_2_out,
       decoder_1_out1, decoder_1_out2;
  wire [1:0] controlled_buffer_2_out, dipswitch_1_sw2, dipswitch_1_sw4;
  wire [3:0] controlled_buffer_3_out, controlled_buffer_8_out, controlled_buffer_10_out,
       controlled_buffer_11_out, controlled_buffer_13_out, controlled_buffer_14_out,
       controlled_buffer_16_out, controlled_buffer_17_out, controlled_buffer_19_out, d_ff_4_q, d_ff_8_q,
       d_ff_12_q, d_ff_16_q, decoder_2_out0, demultiplexer_1_out0, dipswitch_1_sw8, ram_1_data;

  RAM #(.addrWidth(4), .dataWidth(4), .databus("bidir")) ram_1 (
    .addr(controlled_buffer_3_out), .we(controlled_buffer_4_out), .oe(controlled_buffer_1_out),
    .clk(button_1_out), .data(ram_1_data));
  Decoder #(.enable("false"), .select(2)) decoder_1 (
    .out1(decoder_1_out1), .out2(decoder_1_out2), .sel(dipswitch_1_sw2));  // open: out0, out3
  DipSwitch dipswitch_1 (
    .sw1(dipswitch_1_sw2[1]), .sw2(dipswitch_1_sw2[0]), .sw3(dipswitch_1_sw4[1]), .sw4(dipswitch_1_sw4[0]),
    .sw5(dipswitch_1_sw8[3]), .sw6(dipswitch_1_sw8[2]), .sw7(dipswitch_1_sw8[1]), .sw8(dipswitch_1_sw8[0]));
  assign controlled_buffer_1_out = decoder_1_out1 ? decoder_1_out1 : 1'bz;  // Controlled_Buffer controlled_buffer_1
  assign controlled_buffer_2_out = decoder_1_out1 ? dipswitch_1_sw4 : 2'bz;  // Controlled_Buffer controlled_buffer_2
  assign controlled_buffer_3_out = decoder_1_out1 ? dipswitch_1_sw8 : 4'bz;  // Controlled_Buffer controlled_buffer_3
  assign controlled_buffer_4_out = decoder_1_out2 ? decoder_1_out2 : 1'bz;  // Controlled_Buffer controlled_buffer_4
  assign controlled_buffer_1_out = controlled_buffer_5_out ? ~controlled_buffer_5_out : 1'bz;  // Controlled_Inverter controlled_inverter_1
  assign controlled_buffer_5_out = decoder_1_out2 ? decoder_1_out2 : 1'bz;  // Controlled_Buffer controlled_buffer_5
  assign controlled_buffer_2_out = decoder_1_out2 ? dipswitch_1_sw4 : 2'bz;  // Controlled_Buffer controlled_buffer_6
  assign controlled_buffer_3_out = decoder_1_out2 ? dipswitch_1_sw8 : 4'bz;  // Controlled_Buffer controlled_buffer_7
  buf buffer_1 (buffer_1_out, controlled_inverter_2_out);
  assign controlled_inverter_2_out = controlled_buffer_5_out ? ~controlled_buffer_1_out : 1'bz;  // Controlled_Inverter controlled_inverter_2
  Decoder #(.select(2)) decoder_2 (
    .out0(decoder_2_out0[0]), .out1(decoder_2_out0[1]), .out2(decoder_2_out0[2]), .out3(decoder_2_out0[3]),
    .sel(controlled_buffer_2_out), .en(controlled_inverter_2_out));
  Demultiplexer #(.enable("true"), .select(2)) demultiplexer_1 (
    .out0(demultiplexer_1_out0[0]), .out1(demultiplexer_1_out0[1]), .out2(demultiplexer_1_out0[2]),
    .out3(demultiplexer_1_out0[3]), .in(button_1_out), .sel(controlled_buffer_2_out),
    .en(controlled_inverter_2_out));
  Button button_1 (.out(button_1_out));
  Hex_Digit_Display hex_digit_display_1 (.value(ram_1_data));  // open: dp
  assign controlled_buffer_8_out = decoder_2_out0[0] ? ram_1_data : 4'bz;  // Controlled_Buffer controlled_buffer_8
  Controlled_Inverter controlled_inverter_3 ();  // open: in, out, en
  buf buffer_2 (buffer_2_out, buffer_1_out);
  D_Flip_Flop d_ff_1 (
    .D(controlled_buffer_8_out[3]), .clk(demultiplexer_1_out0[0]), .Q(d_ff_4_q[3]));  // open: Qn, preset, reset
  D_Flip_Flop d_ff_2 (
    .D(controlled_buffer_8_out[2]), .clk(demultiplexer_1_out0[0]), .Q(d_ff_4_q[2]));  // open: Qn, preset, reset
  D_Flip_Flop d_ff_3 (
    .D(controlled_buffer_8_out[1]), .clk(demultiplexer_1_out0[0]), .Q(d_ff_4_q[1]));  // open: Qn, preset, reset
  D_Flip_Flop d_ff_4 (
    .D(controlled_buffer_8_out[0]), .clk(demultiplexer_1_out0[0]), .Q(d_ff_4_q[0]));  // open: Qn, preset, reset
  assign ram_1_data = decoder_2_out0[0] ? controlled_buffer_10_out : 4'bz;  // Controlled_Buffer controlled_buffer_9
  assign controlled_buffer_10_out = buffer_2_out ? d_ff_4_q : 4'bz;  // Controlled_Buffer controlled_buffer_10
  assign controlled_buffer_11_out = decoder_2_out0[1] ? ram_1_data : 4'bz;  // Controlled_Buffer controlled_buffer_11
  D_Flip_Flop d_ff_5 (
    .D(controlled_buffer_11_out[3]), .clk(demultiplexer_1_out0[1]), .Q(d_ff_8_q[3]));  // open: Qn, preset, reset
  D_Flip_Flop d_ff_6 (
    .D(controlled_buffer_11_out[2]), .clk(demultiplexer_1_out0[1]), .Q(d_ff_8_q[2]));  // open: Qn, preset, reset
  D_Flip_Flop d_ff_7 (
    .D(controlled_buffer_11_out[1]), .clk(demultiplexer_1_out0[1]), .Q(d_ff_8_q[1]));  // open: Qn, preset, reset
  D_Flip_Flop d_ff_8 (
    .D(controlled_buffer_11_out[0]), .clk(demultiplexer_1_out0[1]), .Q(d_ff_8_q[0]));  // open: Qn, preset, reset
  assign ram_1_data = decoder_2_out0[1] ? controlled_buffer_13_out : 4'bz;  // Controlled_Buffer controlled_buffer_12
  assign controlled_buffer_13_out = buffer_3_out ? d_ff_8_q : 4'bz;  // Controlled_Buffer controlled_buffer_13
  buf buffer_3 (buffer_3_out, controlled_inverter_2_out);
  assign controlled_buffer_14_out = decoder_2_out0[2] ? ram_1_data : 4'bz;  // Controlled_Buffer controlled_buffer_14
  D_Flip_Flop d_ff_9 (
    .D(controlled_buffer_14_out[3]), .clk(demultiplexer_1_out0[2]), .Q(d_ff_12_q[3]));  // open: Qn, preset, reset
  D_Flip_Flop d_ff_10 (
    .D(controlled_buffer_14_out[2]), .clk(demultiplexer_1_out0[2]), .Q(d_ff_12_q[2]));  // open: Qn, preset, reset
  D_Flip_Flop d_ff_11 (
    .D(controlled_buffer_14_out[1]), .clk(demultiplexer_1_out0[2]), .Q(d_ff_12_q[1]));  // open: Qn, preset, reset
  D_Flip_Flop d_ff_12 (
    .D(controlled_buffer_14_out[0]), .clk(demultiplexer_1_out0[2]), .Q(d_ff_12_q[0]));  // open: Qn, preset, reset
  assign ram_1_data = decoder_2_out0[2] ? controlled_buffer_16_out : 4'bz;  // Controlled_Buffer controlled_buffer_15
  assign controlled_buffer_16_out = buffer_4_out ? d_ff_12_q : 4'bz;  // Controlled_Buffer controlled_buffer_16
  buf buffer_4 (buffer_4_out, buffer_1_out);
  assign controlled_buffer_17_out = decoder_2_out0[3] ? ram_1_data : 4'bz;  // Controlled_Buffer controlled_buffer_17
  assign ram_1_data = decoder_2_out0[3] ? controlled_buffer_19_out : 4'bz;  // Controlled_Buffer controlled_buffer_18
  assign controlled_buffer_19_out = buffer_5_out ? d_ff_16_q : 4'bz;  // Controlled_Buffer controlled_buffer_19
  buf buffer_5 (buffer_5_out, buffer_1_out);
  D_Flip_Flop d_ff_13 (
    .D(controlled_buffer_17_out[3]), .clk(demultiplexer_1_out0[3]), .Q(d_ff_16_q[3]));  // open: Qn, preset, reset
  D_Flip_Flop d_ff_14 (
    .D(controlled_buffer_17_out[2]), .clk(demultiplexer_1_out0[3]), .Q(d_ff_16_q[2]));  // open: Qn, preset, reset
  D_Flip_Flop d_ff_15 (
    .D(controlled_buffer_17_out[1]), .clk(demultiplexer_1_out0[3]), .Q(d_ff_16_q[1]));  // open: Qn, preset, reset
  D_Flip_Flop d_ff_16 (
    .D(controlled_buffer_17_out[0]), .clk(demultiplexer_1_out0[3]), .Q(d_ff_16_q[0]));  // open: Qn, preset, reset

  // Notes on the sheet:
  //   10 [REG_ADDR] [RAM_ADDR] For loading into ram for register (STORE)
  //   01 [REG_ADDR] [RAM_ADDR] For Loading into a register from ram (LOAD)
  //   buffer_2 drives only 1 and floats otherwise
  //   buffer_3 drives only 1 and floats otherwise
  //   buffer_4 drives only 1 and floats otherwise
  //   buffer_5 drives only 1 and floats otherwise
endmodule
