// Logisim project RegisterV2.circ as structural Verilog: 1 circuit, main circuit main
module main (
);

  wire and_1_out, and_2_out, and_3_out, and_4_out, and_5_out, and_6_out, buffer_1_out, buffer_2_out,
       buffer_3_out, buffer_4_out, buffer_5_out, button_1_out, dipswitch_2_sw3, dipswitch_2_sw4, not_1_out,
       not_2_out, not_3_out, not_4_out, not_5_out, undriven_4, undriven_5;
  wire [0:0] undriven, undriven_2;
  wire [1:0] dipswitch_2_sw2;
  wire [3:0] controlled_buffer_1_out, controlled_buffer_2_out, controlled_buffer_3_out,
       controlled_buffer_4_out, controlled_buffer_5_out, controlled_buffer_7_out, controlled_buffer_8_out,
       controlled_buffer_10_out, controlled_buffer_11_out, controlled_buffer_13_out,
       controlled_buffer_14_out, controlled_buffer_16_out, d_ff_4_q, d_ff_8_q, d_ff_12_q, d_ff_16_q,
       d_ff_20_q, decoder_1_out0, demultiplexer_1_out0, dipswitch_1_sw4, undriven_3;

  not not_1 (not_1_out, undriven_5);
  and and_1 (and_1_out, undriven_4, not_1_out);
  assign controlled_buffer_1_out = undriven[0] ? undriven_3 : 4'bz;  // Controlled_Buffer controlled_buffer_1
  D_Flip_Flop d_ff_1 (.D(controlled_buffer_1_out[3]), .clk(undriven_2[0]), .Q(d_ff_4_q[3]));  // open: Qn, preset, reset
  D_Flip_Flop d_ff_2 (.D(controlled_buffer_1_out[2]), .clk(undriven_2[0]), .Q(d_ff_4_q[2]));  // open: Qn, preset, reset
  D_Flip_Flop d_ff_3 (.D(controlled_buffer_1_out[1]), .clk(undriven_2[0]), .Q(d_ff_4_q[1]));  // open: Qn, preset, reset
  D_Flip_Flop d_ff_4 (.D(controlled_buffer_1_out[0]), .clk(undriven_2[0]), .Q(d_ff_4_q[0]));  // open: Qn, preset, reset
  assign controlled_buffer_2_out = undriven[0] ? controlled_buffer_3_out : 4'bz;  // Controlled_Buffer controlled_buffer_2
  assign controlled_buffer_3_out = buffer_1_out ? d_ff_4_q : 4'bz;  // Controlled_Buffer controlled_buffer_3
  buf buffer_1 (buffer_1_out, and_1_out);
  DipSwitch #(.number(4)) dipswitch_1 (
    .sw1(dipswitch_1_sw4[3]), .sw2(dipswitch_1_sw4[2]), .sw3(dipswitch_1_sw4[1]), .sw4(dipswitch_1_sw4[0]));
  assign controlled_buffer_4_out = and_2_out ? dipswitch_1_sw4 : 4'bz;  // Controlled_Buffer controlled_buffer_4
  and and_2 (and_2_out, dipswitch_2_sw3, dipswitch_2_sw4);
  DipSwitch #(.number(4)) dipswitch_2 (
    .sw1(dipswitch_2_sw2[1]), .sw2(dipswitch_2_sw2[0]), .sw3(dipswitch_2_sw3), .sw4(dipswitch_2_sw4));
  Decoder #(.select(2)) decoder_1 (
    .out0(decoder_1_out0[0]), .out1(decoder_1_out0[1]), .out2(decoder_1_out0[2]), .out3(decoder_1_out0[3]),
    .sel(dipswitch_2_sw2), .en(dipswitch_2_sw3));
  Demultiplexer #(.enable("true"), .select(2)) demultiplexer_1 (
    .out0(demultiplexer_1_out0[0]), .out1(demultiplexer_1_out0[1]), .out2(demultiplexer_1_out0[2]),
    .out3(demultiplexer_1_out0[3]), .in(button_1_out), .sel(dipswitch_2_sw2), .en(dipswitch_2_sw3));
  Button button_1 (.out(button_1_out));
  Hex_Digit_Display hex_digit_display_1 (.value(controlled_buffer_4_out));  // open: dp
  assign controlled_buffer_5_out = decoder_1_out0[0] ? controlled_buffer_4_out : 4'bz;  // Controlled_Buffer controlled_buffer_5
  not not_2 (not_2_out, and_2_out);
  assign controlled_buffer_4_out = decoder_1_out0[0] ? controlled_buffer_7_out : 4'bz;  // Controlled_Buffer controlled_buffer_6
  and and_3 (and_3_out, dipswitch_2_sw3, not_2_out);
  assign controlled_buffer_7_out = buffer_2_out ? d_ff_8_q : 4'bz;  // Controlled_Buffer controlled_buffer_7
  buf buffer_2 (buffer_2_out, and_3_out);
  D_Flip_Flop d_ff_5 (
    .D(controlled_buffer_5_out[3]), .clk(demultiplexer_1_out0[0]), .Q(d_ff_8_q[3]));  // open: Qn, preset, reset
  D_Flip_Flop d_ff_6 (
    .D(controlled_buffer_5_out[2]), .clk(demultiplexer_1_out0[0]), .Q(d_ff_8_q[2]));  // open: Qn, preset, reset
  D_Flip_Flop d_ff_7 (
    .D(controlled_buffer_5_out[1]), .clk(demultiplexer_1_out0[0]), .Q(d_ff_8_q[1]));  // open: Qn, preset, reset
  D_Flip_Flop d_ff_8 (
    .D(controlled_buffer_5_out[0]), .clk(demultiplexer_1_out0[0]), .Q(d_ff_8_q[0]));  // open: Qn, preset, reset
  not not_3 (not_3_out, and_2_out);
  and and_4 (and_4_out, dipswitch_2_sw3, not_3_out);
  buf buffer_3 (buffer_3_out, and_4_out);
  assign controlled_buffer_8_out = decoder_1_out0[1] ? controlled_buffer_4_out : 4'bz;  // Controlled_Buffer controlled_buffer_8
  D_Flip_Flop d_ff_9 (
    .D(controlled_buffer_8_out[3]), .clk(demultiplexer_1_out0[1]), .Q(d_ff_12_q[3]));  // open: Qn, preset, reset
  D_Flip_Flop d_ff_10 (
    .D(controlled_buffer_8_out[2]), .clk(demultiplexer_1_out0[1]), .Q(d_ff_12_q[2]));  // open: Qn, preset, reset
  D_Flip_Flop d_ff_11 (
    .D(controlled_buffer_8_out[1]), .clk(demultiplexer_1_out0[1]), .Q(d_ff_12_q[1]));  // open: Qn, preset, reset
  D_Flip_Flop d_ff_12 (
    .D(controlled_buffer_8_out[0]), .clk(demultiplexer_1_out0[1]), .Q(d_ff_12_q[0]));  // open: Qn, preset, reset
  assign controlled_buffer_4_out = decoder_1_out0[1] ? controlled_buffer_10_out : 4'bz;  // Controlled_Buffer controlled_buffer_9
  assign controlled_buffer_10_out = buffer_3_out ? d_ff_12_q : 4'bz;  // Controlled_Buffer controlled_buffer_10
  not not_4 (not_4_out, and_2_out);
  and and_5 (and_5_out, dipswitch_2_sw3, not_4_out);
  assign controlled_buffer_11_out = decoder_1_out0[2] ? controlled_buffer_4_out : 4'bz;  // Controlled_Buffer controlled_buffer_11
  D_Flip_Flop d_ff_13 (
    .D(controlled_buffer_11_out[3]), .clk(demultiplexer_1_out0[2]), .Q(d_ff_16_q[3]));  // open: Qn, preset, reset
  D_Flip_Flop d_ff_14 (
    .D(controlled_buffer_11_out[2]), .clk(demultiplexer_1_out0[2]), .Q(d_ff_16_q[2]));  // open: Qn, preset, reset
  D_Flip_Flop d_ff_15 (
    .D(controlled_buffer_11_out[1]), .clk(demultiplexer_1_out0[2]), .Q(d_ff_16_q[1]));  // open: Qn, preset, reset
  D_Flip_Flop d_ff_16 (
    .D(controlled_buffer_11_out[0]), .clk(demultiplexer_1_out0[2]), .Q(d_ff_16_q[0]));  // open: Qn, preset, reset
  assign controlled_buffer_4_out = decoder_1_out0[2] ? controlled_buffer_13_out : 4'bz;  // Controlled_Buffer controlled_buffer_12
  assign controlled_buffer_13_out = buffer_4_out ? d_ff_16_q : 4'bz;  // Controlled_Buffer controlled_buffer_13
  buf buffer_4 (buffer_4_out, and_5_out);
  not not_5 (not_5_out, and_2_out);
  and and_6 (and_6_out, dipswitch_2_sw3, not_5_out);
  assign controlled_buffer_14_out = decoder_1_out0[3] ? controlled_buffer_4_out : 4'bz;  // Controlled_Buffer controlled_buffer_14
  D_Flip_Flop d_ff_17 (
    .D(controlled_buffer_14_out[3]), .clk(demultiplexer_1_out0[3]), .Q(d_ff_20_q[3]));  // open: Qn, preset, reset
  D_Flip_Flop d_ff_18 (
    .D(controlled_buffer_14_out[2]), .clk(demultiplexer_1_out0[3]), .Q(d_ff_20_q[2]));  // open: Qn, preset, reset
  D_Flip_Flop d_ff_19 (
    .D(controlled_buffer_14_out[1]), .clk(demultiplexer_1_out0[3]), .Q(d_ff_20_q[1]));  // open: Qn, preset, reset
  D_Flip_Flop d_ff_20 (
    .D(controlled_buffer_14_out[0]), .clk(demultiplexer_1_out0[3]), .Q(d_ff_20_q[0]));  // open: Qn, preset, reset
  assign controlled_buffer_4_out = decoder_1_out0[3] ? controlled_buffer_16_out : 4'bz;  // Controlled_Buffer controlled_buffer_15
  assign controlled_buffer_16_out = buffer_5_out ? d_ff_20_q : 4'bz;  // Controlled_Buffer controlled_buffer_16
  buf buffer_5 (buffer_5_out, and_6_out);
  RAM #(.addrWidth(2), .dataWidth(4)) ram_1 ();  // open: addr, we, oe, clk, din, dout

  // Notes on the sheet:
  //   buffer_1 drives only 1 and floats otherwise
  //   buffer_2 drives only 1 and floats otherwise
  //   buffer_3 drives only 1 and floats otherwise
  //   buffer_4 drives only 1 and floats otherwise
  //   buffer_5 drives only 1 and floats otherwise
endmodule
