// Logisim project TTLICS.circ as structural Verilog: 1 circuit, main circuit main
module main (
);

  wire dipswitch_2_p1, dipswitch_4_p1, n74175_1_pin1, n74175_1_pin9, n74175_2_pin1, n74175_2_pin2,
       n74175_2_pin7, n74175_2_pin10, n74175_2_pin15, n74175_3_pin9;
  wire [3:0] dipswitch_1_p4, dipswitch_3_p4, n7486_1_pin8, n74157_1_pin3, n74175_1_pin7, n74175_2_pin13,
       n74283_1_pin4, n74283_1_pin9;

  Hex_Digit_Display hex_digit_display_1 (.value(dipswitch_1_p4));  // open: dp
  // DipSwitch #(.number(4)) dipswitch_1: pin names not known; wires that end beside it: dipswitch_1_p4[3], dipswitch_1_p4[2], dipswitch_1_p4[1], dipswitch_1_p4[0]
  _74175 u_74175_1 (
    .pin1(n74175_1_pin1), .pin2(n74175_1_pin7[2]), .pin4(dipswitch_1_p4[1]), .pin5(dipswitch_1_p4[3]),
    .pin7(n74175_1_pin7[0]), .pin15(n74175_1_pin7[3]), .pin13(dipswitch_1_p4[0]), .pin12(dipswitch_1_p4[2]),
    .pin10(n74175_1_pin7[1]), .pin9(n74175_1_pin9));  // open: pin3, pin6, pin14, pin11
  Hex_Digit_Display hex_digit_display_2 (.value(n74175_2_pin13));  // open: dp
  Clock clock_1 (.out(n74175_1_pin9));
  Hex_Digit_Display hex_digit_display_3 (.value(dipswitch_3_p4));  // open: dp
  _74175 #(.ShowInternalStructure("true")) u_74175_2 (
    .pin1(n74175_2_pin1), .pin2(n74175_2_pin2), .pin4(n74175_2_pin13[1]), .pin5(n74175_2_pin13[3]),
    .pin7(n74175_2_pin7), .pin15(n74175_2_pin15), .pin13(n74175_2_pin13[0]), .pin12(n74175_2_pin13[2]),
    .pin10(n74175_2_pin10), .pin9(n74175_1_pin9));  // open: pin3, pin6, pin14, pin11
  // DipSwitch #(.number(1)) dipswitch_2: pin names not known; wires that end beside it: dipswitch_2_p1
  // DipSwitch #(.number(4)) dipswitch_3: pin names not known; wires that end beside it: dipswitch_3_p4[3], dipswitch_3_p4[2], dipswitch_3_p4[1], dipswitch_3_p4[0]
  _74157 #(.ShowInternalStructure("true")) u_74157_1 (
    .pin1(dipswitch_2_p1), .pin2(dipswitch_3_p4[0]), .pin3(n74157_1_pin3[0]), .pin4(n74175_2_pin13[0]),
    .pin5(dipswitch_3_p4[1]), .pin6(n74157_1_pin3[1]), .pin7(n74175_2_pin13[1]), .pin14(dipswitch_3_p4[3]),
    .pin13(n74157_1_pin3[3]), .pin12(n74175_2_pin13[3]), .pin11(dipswitch_3_p4[2]), .pin10(n74157_1_pin3[2]),
    .pin9(n74175_2_pin13[2]));  // open: pin15
  // DipSwitch #(.number(1)) dipswitch_4: pin names not known; wires that end beside it: dipswitch_4_p1
  Hex_Digit_Display hex_digit_display_4 (.value(n74157_1_pin3));  // open: dp
  _7486 #(.ShowInternalStructure("true")) u_7486_1 (
    .pin1(n74175_2_pin7), .pin2(dipswitch_4_p1), .pin3(n7486_1_pin8[3]), .pin4(n74175_2_pin10),
    .pin5(dipswitch_4_p1), .pin6(n7486_1_pin8[2]), .pin13(n74175_2_pin2), .pin12(dipswitch_4_p1),
    .pin11(n7486_1_pin8[1]), .pin10(n74175_2_pin15), .pin9(dipswitch_4_p1), .pin8(n7486_1_pin8[0]));
  Hex_Digit_Display hex_digit_display_5 (.value(n7486_1_pin8));  // open: dp
  _74283 #(.ShowInternalStructure("true")) u_74283_1 (
    .pin1(n74283_1_pin4[1]), .pin2(n74175_1_pin7[2]), .pin3(n7486_1_pin8[1]), .pin4(n74283_1_pin4[0]),
    .pin5(n7486_1_pin8[0]), .pin6(n74175_1_pin7[3]), .pin7(dipswitch_4_p1), .pin15(n74175_1_pin7[1]),
    .pin14(n7486_1_pin8[2]), .pin13(n74283_1_pin4[2]), .pin12(n7486_1_pin8[3]), .pin11(n74175_1_pin7[0]),
    .pin10(n74283_1_pin4[3]), .pin9(n74283_1_pin9[0]));
  Hex_Digit_Display hex_digit_display_6 (.value({n74283_1_pin9[3:2], n74283_1_pin9[2], n74283_1_pin9[0]}));  // open: dp
  Hex_Digit_Display hex_digit_display_7 (.value(n74283_1_pin4));  // open: dp
  Pull_Resistor pull_resistor_1 (.node(n74283_1_pin9[2]));
  Pull_Resistor pull_resistor_2 (.node(n74283_1_pin9[3]));
  _74175 #(.ShowInternalStructure("true")) u_74175_3 (
    .pin2(n74157_1_pin3[0]), .pin4(n74283_1_pin4[0]), .pin5(n74283_1_pin4[1]), .pin7(n74157_1_pin3[1]),
    .pin15(n74157_1_pin3[2]), .pin13(n74283_1_pin4[2]), .pin12(n74283_1_pin4[3]), .pin10(n74157_1_pin3[3]),
    .pin9(n74175_3_pin9));  // open: pin1, pin3, pin6, pin14, pin11
  not not_1 (n74175_3_pin9, n74175_1_pin9);
  // also tied to VCC on the sheet: {n74175_1_pin1, n74175_2_pin1}
endmodule
