// Logisim project registerttlstack.circ as structural Verilog: 1 circuit, main circuit main
module main (
);

  wire n7419_1_pin2, n7419_1_pin4, n7419_1_pin6, n7419_1_pin11, n7419_1_pin12, n74139_1_pin1, n74139_1_pin2,
       n74139_1_pin3, n74139_1_pin4, n74139_1_pin5, n74139_1_pin6, n74139_1_pin7, n74194_1_pin11,
       n74244_1_pin1, n74244_1_pin2, n74244_1_pin3, n74244_1_pin4, n74244_1_pin5, n74244_1_pin6,
       n74244_1_pin7, n74244_1_pin8, n74244_1_pin9, n74244_1_pin19, pull_resistor_1_node,
       pull_resistor_2_node, pull_resistor_3_node, pull_resistor_4_node;

  Pull_Resistor pull_resistor_1 (.node(pull_resistor_1_node));
  Pull_Resistor pull_resistor_2 (.node(pull_resistor_2_node));
  Pull_Resistor pull_resistor_3 (.node(pull_resistor_3_node));
  Pull_Resistor pull_resistor_4 (.node(pull_resistor_4_node));
  _74139 #(.ShowInternalStructure("true")) u_74139_1 (
    .pin1(n74139_1_pin1), .pin2(n74139_1_pin2), .pin3(n74139_1_pin3), .pin4(n74139_1_pin4),
    .pin5(n74139_1_pin5), .pin6(n74139_1_pin6), .pin7(n74139_1_pin7));  // open: pin15, pin14, pin13, pin12, pin11, pin10, pin9
  // DipSwitch #(.number(2)) dipswitch_1: pin names not known; wires that end beside it: pull_resistor_1_node, pull_resistor_2_node, pull_resistor_3_node, pull_resistor_4_node, n74139_1_pin3, n74139_1_pin2
  // DipSwitch #(.number(1)) dipswitch_2: pin names not known
  _7419 #(.ShowInternalStructure("true")) u_7419_1 (
    .pin1(n74139_1_pin4), .pin2(n7419_1_pin2), .pin3(n74139_1_pin5), .pin4(n7419_1_pin4),
    .pin5(n74139_1_pin6), .pin6(n7419_1_pin6), .pin13(n74139_1_pin7), .pin12(n7419_1_pin12),
    .pin11(n7419_1_pin11), .pin10(n74139_1_pin1));  // open: pin9, pin8
  _74244 #(.ShowInternalStructure("true")) u_74244_1 (
    .pin1(n74244_1_pin1), .pin2(n74244_1_pin2), .pin3(n74244_1_pin3), .pin4(n74244_1_pin4),
    .pin5(n74244_1_pin5), .pin6(n74244_1_pin6), .pin7(n74244_1_pin7), .pin8(n74244_1_pin8),
    .pin9(n74244_1_pin9), .pin19(n74244_1_pin19), .pin18(pull_resistor_4_node), .pin17(pull_resistor_4_node),
    .pin16(pull_resistor_3_node), .pin15(pull_resistor_3_node), .pin14(pull_resistor_2_node),
    .pin13(pull_resistor_2_node), .pin12(pull_resistor_1_node), .pin11(pull_resistor_1_node));
  // DipSwitch #(.number(1)) dipswitch_3: pin names not known; wires that end beside it: n7419_1_pin11, n7419_1_pin12, n7419_1_pin6, n7419_1_pin4
  _74194 #(.ShowInternalStructure("true")) u_74194_1 (
    .pin3(n74244_1_pin9), .pin4(n74244_1_pin7), .pin5(n74244_1_pin5), .pin6(n74244_1_pin3),
    .pin15(n74244_1_pin8), .pin14(n74244_1_pin6), .pin13(n74244_1_pin4), .pin12(n74244_1_pin2),
    .pin11(n74194_1_pin11), .pin10(n74244_1_pin1), .pin9(n74244_1_pin1));  // open: pin1, pin2, pin7
  Clock clock_1 (.out(n74194_1_pin11));
  _7419 #(.ShowInternalStructure("true")) u_7419_2 (
    .pin1(n74244_1_pin1), .pin2(n74244_1_pin19), .pin3(n7419_1_pin2), .pin4(n74244_1_pin1));  // open: pin5, pin6, pin13, pin12, pin11, pin10, pin9, pin8
endmodule
